# Fritzing sketch Jaojao-Cifra_Gudito (saved by Fritzing 0.9.3b)
perfboards: 1

parts:
  Matrix_keypad1 = KEYPAD 4x4
  Part1 = Arduino Mega 2560 (Rev3)
  LED22 = LED - 5mm [color="Red (633nm)" package="5 mm [THT]"]
  LED15 = LED - 5mm [color="Red (633nm)" package="5 mm [THT]"]
  LED20 = LED - 5mm [color="Red (633nm)" package="5 mm [THT]"]
  LED5 = LED - 5mm [color="Red (633nm)" package="5 mm [THT]"]
  LED1 = LED - 5mm [color="Red (633nm)" package="5 mm [THT]"]
  LED13 = LED - 5mm [color="Red (633nm)" package="5 mm [THT]"]
  LED2 = LED - 5mm [color="Red (633nm)" package="5 mm [THT]"]
  LED23 = LED - 5mm [color="Red (633nm)" package="5 mm [THT]"]
  LED4 = LED - 5mm [color="Red (633nm)" package="5 mm [THT]"]
  LED24 = LED - 5mm [color="Red (633nm)" package="5 mm [THT]"]
  LED8 = LED - 5mm [color="Red (633nm)" package="5 mm [THT]"]
  LED10 = LED - 5mm [color="Red (633nm)" package="5 mm [THT]"]
  LED16 = LED - 5mm [color="Red (633nm)" package="5 mm [THT]"]
  LED9 = LED - 5mm [color="Red (633nm)" package="5 mm [THT]"]
  LED7 = LED - 5mm [color="Red (633nm)" package="5 mm [THT]"]
  LED21 = LED - 5mm [color="Red (633nm)" package="5 mm [THT]"]
  LED18 = LED - 5mm [color="Red (633nm)" package="5 mm [THT]"]
  LED12 = LED - 5mm [color="Red (633nm)" package="5 mm [THT]"]
  LED6 = LED - 5mm [color="Red (633nm)" package="5 mm [THT]"]
  LED17 = LED - 5mm [color="Red (633nm)" package="5 mm [THT]"]
  LED19 = LED - 5mm [color="Red (633nm)" package="5 mm [THT]"]
  LED11 = LED - 5mm [color="Red (633nm)" package="5 mm [THT]"]
  LED25 = LED - 5mm [color="Red (633nm)" package="5 mm [THT]"]
  LED3 = LED - 5mm [color="Red (633nm)" package="5 mm [THT]"]
  LED14 = LED - 5mm [color="Red (633nm)" package="5 mm [THT]"]

nets:
  N1: Matrix_keypad1.col1, Part1.D6_PWM
  N2: Matrix_keypad1.col2, Part1.D7_PWM
  N3: Matrix_keypad1.col3, Part1.D8_PWM
  N4: Matrix_keypad1.col4, Part1.D9_PWM
  N5: Matrix_keypad1.row1, Part1.D2_PWM
  N6: Matrix_keypad1.row2, Part1.D3_PWM
  N7: Matrix_keypad1.row3, Part1.D4_PWM
  N8: Matrix_keypad1.row4, Part1.D5_PWM
  N9: Part1.D28, LED1.anode
  N10: Part1.D30, LED2.anode
  N11: Part1.D31, LED3.anode
  N12: Part1.D32, LED4.anode
  N13: Part1.D33, LED5.anode
  N14: Part1.D34, LED6.anode
  N15: Part1.D35, LED7.anode
  N16: Part1.D36, LED8.anode
  N17: Part1.D37, LED9.anode
  N18: Part1.D38, LED10.anode
  N19: Part1.D39, LED11.anode
  N20: Part1.D40, LED12.anode
  N21: Part1.D41, LED13.anode
  N22: Part1.D42, LED14.anode
  N23: Part1.D43, LED15.anode
  N24: Part1.D44, LED16.anode
  N25: Part1.D45, LED17.anode
  N26: Part1.D46, LED18.anode
  N27: Part1.D47, LED19.anode
  N28: Part1.D48, LED20.anode
  N29: Part1.D49, LED21.anode
  N30: Part1.D50, LED22.anode
  N31: Part1.D51, LED23.anode
  N32: Part1.D52, LED24.anode
  N33: Part1.D53, LED25.anode
  N34: Part1.GND, LED22.cathode, LED15.cathode, LED20.cathode, LED5.cathode, LED1.cathode, LED13.cathode, LED2.cathode, LED23.cathode, LED4.cathode, LED24.cathode, LED8.cathode, LED10.cathode, LED16.cathode, LED9.cathode, LED7.cathode, LED21.cathode, LED18.cathode, LED12.cathode, LED6.cathode, LED17.cathode, LED19.cathode, LED11.cathode, LED25.cathode, LED3.cathode, LED14.cathode

custom parts:
  KEYPAD 4x4: Matrix keypad 16 buttons, 4 rows x 4 columns
